# Fritzing sketch YDigi_Puzzle (saved by Fritzing 0.9.9b)
breadboards: 1

parts:
  Part1 = Arduino Mega 2560 (Rev3)
  Grove1 = Grove OLED 128x96
  U1 = 7-SEGMENT-4DIGIT-YOUNGSUN [package=7-segment-4digit-youngsun-longpads]
  RE1 = Rotary Encoder [package=THT]
  Mod1 = Passive Buzzer  # not connected
  R3 = Resistor [tolerance=±5% resistance=220 package="0805 [SMD]"]
  R4 = Resistor [tolerance=±5% resistance=220 package="0805 [SMD]"]
  R5 = Resistor [tolerance=±5% resistance=220 package="0805 [SMD]"]
  R6 = Resistor [tolerance=±5% resistance=220 package="0805 [SMD]"]
  R7 = Resistor [tolerance=±5% resistance=220 package="0805 [SMD]"]
  R9 = Resistor [tolerance=±5% resistance=220 package="0805 [SMD]"]
  R10 = Resistor [tolerance=±5% resistance=220 package="0805 [SMD]"]
  R11 = Resistor [tolerance=±5% resistance=220 package="0805 [SMD]"]
  R12 = Resistor [tolerance=±5% resistance=220 package="0805 [SMD]"]
  R13 = Resistor [tolerance=±5% resistance=220 package="0805 [SMD]"]
  R14 = Resistor [tolerance=±5% resistance=220 package="0805 [SMD]"]
  R15 = Resistor [tolerance=±5% resistance=220 package="0805 [SMD]"]
  R16 = Resistor [tolerance=±5% resistance=220 package="0805 [SMD]"]
  R17 = Resistor [tolerance=±5% resistance=220 package="0805 [SMD]"]

nets:
  N1: Part1.A0, R10.Pin_1
  N2: Part1.A1, R14.Pin_1
  N3: Part1.D21/SCL, Grove1.SCL
  N4: Part1.D20/SDA, Grove1.SDA
  5V: Part1.5V, Grove1.VCC
  N5: Part1.GND, RE1.EncoderPinC
  N6: Part1.D2_PWM, RE1.EncoderPinA
  N7: Part1.D4_PWM, RE1.EncoderPinB
  N8: Part1.D42, R11.Pin_1
  N9: Part1.D43, R15.Pin_1
  N10: Part1.D44, R4.Pin_1
  N11: Part1.D45, R16.Pin_1
  N12: Part1.D46, R3.Pin_1
  N13: Part1.D47, U1.COL-C, R17.Pin_0, R17.Pin_1
  N14: Part1.D48, R7.Pin_0
  N15: Part1.D49, R9.Pin_0
  N16: Part1.D50, R6.Pin_0
  N17: Part1.D51, R13.Pin_0
  N18: Part1.D52, R5.Pin_0
  N19: Part1.D53, R12.Pin_0
  N20: U1.DIG2, R5.Pin_1
  N21: U1.D, R6.Pin_1
  N22: U1.COL-A, R7.Pin_1
  N23: U1.E, R3.Pin_0
  N24: U1.DIG3, R4.Pin_0
  N25: U1.DP, R11.Pin_0
  N26: U1.DIG4, R10.Pin_0
  N27: U1.APOS-C, R14.Pin_0
  N28: U1.APOS-A, R15.Pin_0
  N29: U1.F, R16.Pin_0
  N30: U1.C, R9.Pin_1
  N31: U1.A, R13.Pin_1
  N32: U1.G, R12.Pin_1
